# Fritzing sketch monitor1 (saved by Fritzing 0.9.3b)
breadboards: 1

parts:
  Arduino_Nano = Arduino Nano (Rev3.0)
  J2-ws = Generic connector 1 Pin [form=male package=THT]
  J4-sw = Generic connector 1 Pin [form=male package=THT]
  U2 = Generic-4PinEdit [package=THT]
  +12V = Generic connector 1 Pin [form=male package=THT]
  GND = Generic connector 1 Pin [form=male package=THT]
  U3 = mystery part, 5 pins [chip_label=Relais]
  D1 = Rectifier Diode [part_number=1N4001 package="300 mil [THT]"]
  D2 = Rectifier Diode [part_number=1N4001 package="300 mil [THT]"]
  D+_Kühlschrank = Generic connector 1 Pin [form=male package=THT]
  original_D+ = Generic connector 1 Pin [form=male package=THT]
  original_D+_2 = Generic connector 1 Pin [form=male package=THT]
  R1 = Resistor [tolerance=±5% resistance=1k package=THT]
  Q2 = NPN-Transistor [part_number=BC337 package="TO92 [THT]"]
  R5 = Resistor [tolerance=±5% resistance=10k package=THT]
  LED1 = LED - 5mm [color="Green (560nm)" package="5 mm [THT]"]
  R6 = Resistor [tolerance=±5% resistance=220 package=THT]
  C1 = Electrolytic Capacitor [capacitance=50µF package="100 mil [THT, electrolytic]"]
  S1 = Pushbutton [package=THT]
  D+ = Generic connector 1 Pin [form=male package=THT]

nets:
  N1: Arduino_Nano.RESET, S1.leg0
  GND: Arduino_Nano.GND, J4-sw.pin1, U2.GND_OUT, U3.pin3, Q2.E, C1.-
  N2: Arduino_Nano.D2, R1.Pin_1
  N3: Arduino_Nano.D4, U3.pin2
  N4: Arduino_Nano.D5, R5.Pin_0
  N5: Arduino_Nano.VIN, U2.+5
  N6: Arduino_Nano.5V, U3.pin1, R6.Pin_0
  N7: J2-ws.pin1, R1.Pin_0
  N8: U2.+12V, +12V.pin1, U3.pin4
  N9: U2.GND_IN, GND.pin1
  N10: U3.pin5, D+.pin1
  N11: D1.cathode, D2.cathode, D+_Kühlschrank.pin1
  N12: D1.anode, original_D+.pin1
  N13: D2.anode, original_D+_2.pin1
  N14: Q2.B, R5.Pin_1
  N15: Q2.C, LED1.cathode
  N16: LED1.anode, R6.Pin_1
  N17: C1.+, S1.leg1

notes:
  JST-PH 2.00mm pitch 4-pin connector female cable
  Victron MPPT
  ChargeMonitor 2019/03/31
  6V
  close normal/open prog

custom parts:
  Generic connector 1 Pin: Generic male header
  Generic-4PinEdit: 4Pin edit pin labels
